// Logisim project alu.circ as structural Verilog: 2 circuits, main circuit main
module main (
  input  Sub,
  input  Cin,
  input  [2:0] in_3,
  input  A,
  input  B,
  input  Less,
  output RESULT,
  output out_8,
  output Cout
);

  wire adder_1_cout, and_1_out, divider_1_out, divider_1_rem, multiplier_1_cout, multiplier_1_out, nor_1_out,
       or_2_out, xor_1_out, xor_2_out;

  xor xor_1 (xor_1_out, B, Sub);
  or or_1 (Cout, adder_1_cout, multiplier_1_cout);
  and and_1 (and_1_out, A, B);
  or or_2 (or_2_out, A, B);
  xor xor_2 (xor_2_out, A, B);
  nor nor_1 (nor_1_out, A, B);
  Adder #(.width(1)) adder_1 (.a(A), .b(xor_1_out), .out(out_8), .cin(Cin), .cout(adder_1_cout));
  Multiplier #(.width(1)) multiplier_1 (.a(A), .b(B), .out(multiplier_1_out), .cin(Cin), .cout(multiplier_1_cout));
  Divider #(.width(1)) divider_1 (.a(A), .b(B), .out(divider_1_out), .rem(divider_1_rem));  // open: upper
  Multiplexer #(.select(3), .enable("false")) multiplexer_1 (
    .in0(and_1_out), .in1(or_2_out), .in2(xor_2_out), .in3(nor_1_out), .in4(out_8), .in5(multiplier_1_out),
    .in6(divider_1_out), .in7(divider_1_rem), .out(RESULT), .sel(in_3));
endmodule

module ALU_222 (
  input  [2:0] in_1,
  input  in_2,
  input  [7:0] in_3,
  input  [7:0] in_4,
  output [7:0] out_5,
  output [7:0] out_6,
  output [7:0] out_7,
  output [7:0] out_8
);

  wire main_1_cout, main_2_cout, main_3_cout, main_4_cout, main_5_cout, main_6_cout, main_7_cout,
       main_8_out_8;

  Multiplier multiplier_1 (.a(in_3), .b(in_4), .out(out_6));  // open: cin, cout
  Divider divider_1 (.a(in_3), .b(in_4), .out(out_7), .rem(out_8));  // open: upper
  main main_1 (
    .A(in_3[0]), .B(in_4[0]), .Less(main_8_out_8), .RESULT(out_5[0]), .Sub(in_2), .Cin(in_2), .in_3(in_1),
    .Cout(main_1_cout));  // open: out_8
  main main_2 (
    .A(in_3[1]), .B(in_4[1]), .Less(1'b0), .RESULT(out_5[1]), .Sub(in_2), .Cin(main_1_cout), .in_3(in_1),
    .Cout(main_2_cout));  // open: out_8
  main main_3 (
    .A(in_3[2]), .B(in_4[2]), .Less(1'b0), .RESULT(out_5[2]), .Sub(in_2), .Cin(main_2_cout), .in_3(in_1),
    .Cout(main_3_cout));  // open: out_8
  main main_4 (
    .A(in_3[3]), .B(in_4[3]), .Less(1'b0), .RESULT(out_5[3]), .Sub(in_2), .Cin(main_3_cout), .in_3(in_1),
    .Cout(main_4_cout));  // open: out_8
  main main_5 (
    .A(in_3[4]), .B(in_4[4]), .Less(1'b0), .RESULT(out_5[4]), .Sub(in_2), .Cin(main_4_cout), .in_3(in_1),
    .Cout(main_5_cout));  // open: out_8
  main main_6 (
    .A(in_3[5]), .B(in_4[5]), .Less(1'b0), .RESULT(out_5[5]), .Sub(in_2), .Cin(main_5_cout), .in_3(in_1),
    .Cout(main_6_cout));  // open: out_8
  main main_7 (
    .A(in_3[6]), .B(in_4[6]), .Less(1'b0), .RESULT(out_5[6]), .Sub(in_2), .Cin(main_6_cout), .in_3(in_1),
    .Cout(main_7_cout));  // open: out_8
  main main_8 (
    .A(in_3[7]), .B(in_4[7]), .Less(1'b0), .RESULT(out_5[7]), .Sub(in_2), .Cin(main_7_cout), .in_3(in_1),
    .out_8(main_8_out_8));  // open: Cout
endmodule
