// Logisim project alu_8.circ as structural Verilog
module alu_8bt (
  input  Cin,
  input  [3:0] in_2,
  input  [7:0] A,
  input  [7:0] B,
  output [7:0] RESULT,
  output Cout,
  output [7:0] out_7
);

  wire [7:0] and_1_out, divider_1_out, divider_1_rem, multiplier_1_out, nor_1_out, or_1_out,
       subtractor_1_out, xor_1_out;

  assign and_1_out = A & B;  // AND_Gate and_1, 8 bits wide
  assign or_1_out = A | B;  // OR_Gate or_1, 8 bits wide
  assign xor_1_out = A ^ B;  // XOR_Gate xor_1, 8 bits wide
  assign nor_1_out = ~(A | B);  // NOR_Gate nor_1, 8 bits wide
  Adder adder_1 (.a(A), .b(B), .out(out_7), .cin(Cin), .cout(Cout));
  Subtractor subtractor_1 (.a(A), .b(B), .out(subtractor_1_out));  // open: bin, bout
  Multiplier multiplier_1 (.a(A), .b(B), .out(multiplier_1_out));  // open: cin, cout
  Divider divider_1 (.a(A), .b(B), .out(divider_1_out), .rem(divider_1_rem));  // open: upper
  Multiplexer #(.select(4), .width(8), .enable("false")) multiplexer_1 (
    .in0(and_1_out), .in1(or_1_out), .in2(xor_1_out), .in3(nor_1_out), .in4(out_7), .in5(subtractor_1_out),
    .in6(multiplier_1_out), .in7(divider_1_out), .in8(divider_1_rem), .out(RESULT), .sel(in_2));  // open: in9, in10, in11, in12, in13, in14, in15
endmodule

module main (
  input  [3:0] in_1,
  input  [7:0] in_2,
  input  [7:0] in_3,
  output [7:0] out_4
);

  alu_8bt alu_8bt_1 (.A(in_2), .B(in_3), .RESULT(out_4), .in_2(in_1));  // open: Cin, Cout, out_7
endmodule
