// Logisim project sm1.circ as structural Verilog: 1 circuit, main circuit main
module main (
);

  wire and_1_out, and_2_out, and_3_out, clock_1_out, comparator_1_eq, comparator_2_eq, comparator_3_eq,
       comparator_4_eq, comparator_5_lt, comparator_6_eq, controlled_buffer_1_out, not_1_out, not_2_out,
       not_3_out, not_4_out, or_1_out;
  wire [7:0] counter_1_q, divider_1_out, divider_1_rem, divider_2_rem, undriven;

  // Probe on 8'hf
  not not_1 (not_1_out, comparator_4_eq);
  not not_2 (not_2_out, comparator_1_eq);
  not not_3 (not_3_out, comparator_2_eq);
  Comparator #(.mode("unsigned")) comparator_1 (.a(8'hf), .b({8{1'b0}}), .eq(comparator_1_eq));  // open: gt, lt
  // Probe on comparator_1_eq
  // Probe on comparator_2_eq
  Comparator #(.mode("unsigned")) comparator_2 (.a(8'hf), .b(8'h1), .eq(comparator_2_eq));  // open: gt, lt
  and and_1 (and_1_out, not_2_out, not_3_out, comparator_3_eq);
  and and_2 (and_2_out, not_1_out, not_2_out, not_3_out, not_4_out);
  Comparator #(.mode("unsigned")) comparator_3 (.a(8'hf), .b(8'h2), .eq(comparator_3_eq));  // open: gt, lt
  or or_1 (or_1_out, and_1_out, and_2_out);
  // Probe on divider_1_rem
  LED led_1 (.in(or_1_out));
  // Probe on divider_1_out
  Divider divider_1 (.a(8'hf), .b(8'h2), .out(divider_1_out), .rem(divider_1_rem));  // open: upper
  Comparator #(.mode("unsigned")) comparator_4 (
    .a(divider_1_rem), .b({8{1'b0}}), .eq(comparator_4_eq));  // open: gt, lt
  assign controlled_buffer_1_out = and_3_out ? clock_1_out : 1'bz;  // Controlled_Buffer controlled_buffer_1
  Clock #(.highDuration(1000), .lowDuration(1000)) clock_1 (.out(clock_1_out));
  and and_3 (and_3_out, not_4_out, comparator_5_lt);
  // Probe on divider_2_rem
  Counter counter_1 (.D(8'h2), .Q(counter_1_q), .clk(controlled_buffer_1_out));  // open: load, count, carry, clr
  Controlled_Buffer controlled_buffer_2 ();  // open: in, out, en
  Divider divider_2 (.a(8'hf), .b(undriven), .rem(divider_2_rem));  // open: out, upper
  // Probe on counter_1_q
  Comparator #(.mode("unsigned")) comparator_5 (
    .a(counter_1_q), .b(divider_1_out), .lt(comparator_5_lt));  // open: gt, eq
  not not_4 (not_4_out, comparator_6_eq);
  Comparator #(.mode("unsigned")) comparator_6 (
    .a(divider_2_rem), .b({8{1'b0}}), .eq(comparator_6_eq));  // open: gt, lt
endmodule
